# Fritzing sketch Scantastrophe_Breadboard_Design (saved by Fritzing 0.9.10b)
breadboards: 3

parts:
  Part1 = Arduino Due (Rev2b)
  Part2 = Adafruit TCS34725 RGB Color Sensor [part_number="Adafruit #1334"]
  Part3 = Adafruit TCS34725 RGB Color Sensor [part_number="Adafruit #1334"]
  Part4 = Adafruit TCS34725 RGB Color Sensor [part_number="Adafruit #1334"]
  Part5 = Adafruit TCS34725 RGB Color Sensor [part_number="Adafruit #1334"]
  Part6 = Adafruit TCS34725 RGB Color Sensor [part_number="Adafruit #1334"]
  Part7 = Adafruit TCS34725 RGB Color Sensor [part_number="Adafruit #1334"]
  Part8 = Adafruit TCS34725 RGB Color Sensor [part_number="Adafruit #1334"]
  Part9 = Adafruit TCS34725 RGB Color Sensor [part_number="Adafruit #1334"]
  Part10 = Adafruit TCA9548A
  S1 = Momentary Switch [package=ksa_sealed_tac_switch]
  R1 = Resistor [tolerance=±5% resistance=4700 package="0603 [SMD]"]
  R2 = Resistor [tolerance=±5% resistance=4700 package="0603 [SMD]"]
  R3 = Resistor [tolerance=±5% resistance=4700 package="0603 [SMD]"]
  R4 = Resistor [tolerance=±5% resistance=4700 package="0603 [SMD]"]
  R5 = Resistor [tolerance=±5% resistance=4700 package="0603 [SMD]"]
  R6 = Resistor [tolerance=±5% resistance=4700 package="0603 [SMD]"]
  R7 = Resistor [tolerance=±5% resistance=4700 package="0603 [SMD]"]
  R8 = Resistor [tolerance=±5% resistance=4700 package="0603 [SMD]"]
  R9 = Resistor [tolerance=±5% resistance=4700 package="0603 [SMD]"]
  R10 = Resistor [tolerance=±5% resistance=4700 package="0603 [SMD]"]
  R11 = Resistor [tolerance=±5% resistance=4700 package="0603 [SMD]"]
  R12 = Resistor [tolerance=±5% resistance=4700 package="0603 [SMD]"]
  R13 = Resistor [tolerance=±5% resistance=4700 package="0603 [SMD]"]
  R14 = Resistor [tolerance=±5% resistance=4700 package="0603 [SMD]"]
  R15 = Resistor [tolerance=±5% resistance=4700 package="0603 [SMD]"]
  R16 = Resistor [tolerance=±5% resistance=4700 package="0603 [SMD]"]
  R17 = Resistor [tolerance=±5% resistance=4700 package="0603 [SMD]"]
  Part11 = Adafruit TCS34725 RGB Color Sensor [part_number="Adafruit #1334"]
  Part12 = Adafruit TCS34725 RGB Color Sensor [part_number="Adafruit #1334"]
  Part13 = Adafruit TCS34725 RGB Color Sensor [part_number="Adafruit #1334"]
  Part14 = Adafruit TCS34725 RGB Color Sensor [part_number="Adafruit #1334"]
  Part15 = Adafruit TCS34725 RGB Color Sensor [part_number="Adafruit #1334"]
  Part16 = Adafruit TCS34725 RGB Color Sensor [part_number="Adafruit #1334"]
  Part17 = Adafruit TCS34725 RGB Color Sensor [part_number="Adafruit #1334"]
  Part18 = Adafruit TCS34725 RGB Color Sensor [part_number="Adafruit #1334"]
  Part19 = Adafruit TCA9548A
  R18 = Resistor [tolerance=±5% resistance=4700 package="0603 [SMD]"]
  R19 = Resistor [tolerance=±5% resistance=4700 package="0603 [SMD]"]
  R20 = Resistor [tolerance=±5% resistance=4700 package="0603 [SMD]"]
  R21 = Resistor [tolerance=±5% resistance=4700 package="0603 [SMD]"]
  R22 = Resistor [tolerance=±5% resistance=4700 package="0603 [SMD]"]
  R23 = Resistor [tolerance=±5% resistance=4700 package="0603 [SMD]"]
  R24 = Resistor [tolerance=±5% resistance=4700 package="0603 [SMD]"]
  R25 = Resistor [tolerance=±5% resistance=4700 package="0603 [SMD]"]
  R26 = Resistor [tolerance=±5% resistance=4700 package="0603 [SMD]"]
  R27 = Resistor [tolerance=±5% resistance=4700 package="0603 [SMD]"]
  R28 = Resistor [tolerance=±5% resistance=4700 package="0603 [SMD]"]
  R29 = Resistor [tolerance=±5% resistance=4700 package="0603 [SMD]"]
  R30 = Resistor [tolerance=±5% resistance=4700 package="0603 [SMD]"]
  R31 = Resistor [tolerance=±5% resistance=4700 package="0603 [SMD]"]
  R32 = Resistor [tolerance=±5% resistance=4700 package="0603 [SMD]"]
  R33 = Resistor [tolerance=±5% resistance=4700 package="0603 [SMD]"]

nets:
  +3V3: Part1.IOREF, Part2.+3V3, Part3.+3V3, Part4.+3V3, Part5.+3V3, Part6.+3V3, Part7.+3V3, Part8.+3V3, Part9.+3V3, Part10.VCC, S1.3, R2.Pin_0, R3.Pin_0, R4.Pin_0, R5.Pin_0, R6.Pin_0, R7.Pin_0, R8.Pin_0, R9.Pin_0, R10.Pin_0, R11.Pin_0, R12.Pin_0, R13.Pin_0, R14.Pin_0, R15.Pin_0, R16.Pin_0, R17.Pin_0, Part11.+3V3, Part12.+3V3, Part13.+3V3, Part14.+3V3, Part15.+3V3, Part16.+3V3, Part17.+3V3, Part18.+3V3, Part19.VCC, Part19.A0, R18.Pin_0, R19.Pin_0, R20.Pin_0, R21.Pin_0, R22.Pin_0, R23.Pin_0, R24.Pin_0, R25.Pin_0, R26.Pin_0, R27.Pin_0, R28.Pin_0, R29.Pin_0, R30.Pin_0, R31.Pin_0, R32.Pin_0, R33.Pin_0
  GND: Part1.GND, Part2.GND, Part3.GND, Part4.GND, Part5.GND, Part6.GND, Part7.GND, Part8.GND, Part9.GND, Part10.GND, Part10.A0, Part10.A1, Part10.A2, R1.Pin_1, Part11.GND, Part12.GND, Part13.GND, Part14.GND, Part15.GND, Part16.GND, Part17.GND, Part18.GND, Part19.GND, Part19.A1, Part19.A2
  N1: Part1.D13_PWM, Part2.LED_EN, Part3.LED_EN, Part4.LED_EN, Part5.LED_EN, Part6.LED_EN, Part7.LED_EN, Part8.LED_EN, Part9.LED_EN, Part11.LED_EN, Part12.LED_EN, Part13.LED_EN, Part14.LED_EN, Part15.LED_EN, Part16.LED_EN, Part17.LED_EN, Part18.LED_EN
  N2: Part1.D2_PWM, Part10.INPUTSCL
  N3: Part1.D3_PWM, Part10.INPUTSDA
  N4: Part1.D4_PWM/SS1, Part19.INPUTSCL
  N5: Part1.D5_PWM, Part19.INPUTSDA
  N6: Part1.D7_PWM, S1.2
  N7: Part2.SCL, Part10.3SCL, R14.Pin_1
  N8: Part2.SDA, Part10.3SDA, R15.Pin_1
  N9: Part3.SCL, Part10.7SCL, R6.Pin_1
  N10: Part3.SDA, Part10.7SDA, R7.Pin_1
  N11: Part4.SCL, Part10.2SCL, R16.Pin_1
  N12: Part4.SDA, Part10.2SDA, R17.Pin_1
  N13: Part5.SCL, Part10.6SCL, R8.Pin_1
  N14: Part5.SDA, Part10.6SDA, R9.Pin_1
  N15: Part6.SCL, Part10.5SCL, R10.Pin_1
  N16: Part6.SDA, Part10.5SDA, R11.Pin_1
  N17: Part7.SCL, Part10.1SCL, R3.Pin_1
  N18: Part7.SDA, Part10.1SDA, R2.Pin_1
  N19: Part8.SCL, Part10.0SCL, R4.Pin_1
  N20: Part8.SDA, Part10.0SDA, R5.Pin_1
  N21: Part9.SCL, Part10.4SCL, R12.Pin_1
  N22: Part9.SDA, Part10.4SDA, R13.Pin_1
  N23: S1.1, R1.Pin_0
  N24: Part11.SCL, Part19.1SCL, R28.Pin_1
  N25: Part11.SDA, Part19.1SDA, R30.Pin_1
  N26: Part12.SCL, Part19.0SCL, R27.Pin_1
  N27: Part12.SDA, Part19.0SDA, R26.Pin_1
  N28: Part13.SCL, Part19.5SCL, R24.Pin_1
  N29: Part13.SDA, Part19.5SDA, R19.Pin_1
  N30: Part14.SCL, Part19.4SCL, R18.Pin_1
  N31: Part14.SDA, Part19.4SDA, R20.Pin_1
  N32: Part15.SCL, Part19.3SCL, R22.Pin_1
  N33: Part15.SDA, Part19.3SDA, R21.Pin_1
  N34: Part16.SCL, Part19.6SCL, R33.Pin_1
  N35: Part16.SDA, Part19.6SDA, R29.Pin_1
  N36: Part17.SCL, Part19.7SCL, R31.Pin_1
  N37: Part17.SDA, Part19.7SDA, R32.Pin_1
  N38: Part18.SCL, Part19.2SCL, R25.Pin_1
  N39: Part18.SDA, Part19.2SDA, R23.Pin_1

custom parts:
  Adafruit TCS34725 RGB Color Sensor: Your electronics can now see in dazzling color with this lovely color light sensor. We found the best color sensor on the market, the TCS34725, which has RGB and Clear light sensing elements. An IR blocking filter, integrated on-chip and localized to the color sensing photodiodes, minimizes the IR spectral component of the incoming light and allows color measurements to be made accurately. The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
  Adafruit TCA9548A: You just found the perfect I2C sensor, and you want to wire up two or three or more of them to your Arduino when you realize "Uh oh, this chip has a fixed I2C address, and from what I know about I2C, you cannot have two devices with the same address on the same SDA/SCL pins!" Are you out of luck? You would be, if you didn't have this ultra-cool TCA9548A 1-to-8 I2C multiplexer! Finally, a way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
